# Fritzing sketch LORA_END_DEVICE (saved by Fritzing 0.9.3b)
circuit board: 6.9cm x 2.6cm

parts:
  RFM95W = RFM69HCW ISM Transciever
  H1 = XBEE-1 [package=xbee-1]
  u_fl = U.FL [package=u.fl]
  28_DIP = atmega328 [package=dip]
  J1 = female pin header, 4 pins [form="♀ (female)"]
  XTAL = Crystal [frequency="16 Mhz" package=THT]
  LED = LED - 3mm [color="Red (633nm)" package="3 mm [THT]"]

nets:
  GND: RFM95W.1_GND, RFM95W.10_GND, H1.GND, u_fl.GND, 28_DIP.GND, J1.pin2
  N1: RFM95W.2_MISO, 28_DIP.D12
  N2: RFM95W.3_MOSI, 28_DIP.D11_(PWM)
  N3: RFM95W.4_SCK, 28_DIP.D13
  N4: RFM95W.5_NSS_(CS), 28_DIP.D9_(PWM)
  N5: RFM95W.6_RESET, 28_DIP.D10_(PWM)
  N6: RFM95W.9_ANT, u_fl.SIGNAL
  VDD: RFM95W.13_3.3V, H1.VDD, 28_DIP.VCC, 28_DIP.AVCC, J1.pin1
  N7: RFM95W.14_DIO0, 28_DIP.D2
  N8: RFM95W.15_DIO1, 28_DIP.D3_(PWM)
  N9: H1.DOUT, 28_DIP.D1_(TX)
  N10: H1.DIN, 28_DIP.D0_(RX)
  N11: 28_DIP.RESET, J1.pin4
  N12: 28_DIP.XLAT1, XTAL.pin_0
  N13: 28_DIP.XLAT2, XTAL.pin_1
  N14: 28_DIP.D6_(PWM), LED.anode
  N15: 28_DIP.D7, LED.cathode

notes:
  H2

custom parts:
  RFM69HCW ISM Transciever: RF Transceiver by Hope RF. Well supported Arduino libraries are available. This ISM band transceiver is available in several frequencies e.g. 433MHz and 915MHz and it is also available in various feature versions.
